// Logisim project Other-Modules.circ as structural Verilog: 10 circuits, main circuit 8DFF
module _8DFF (
  input  Enable,
  input  Clear,
  input  Clock,
  input  [7:0] I,
  output [7:0] Q
);

  Hex_Digit_Display hex_digit_display_1 (.value(I[3:0]));  // open: dp
  Hex_Digit_Display hex_digit_display_2 (.value(I[7:4]));  // open: dp
  D_Flip_Flop d_ff_1 (.clk(Clock), .D(I[0]), .Q(Q[0]), .en(Enable), .reset(Clear));  // open: Qn, preset
  D_Flip_Flop d_ff_2 (.clk(Clock), .D(I[1]), .Q(Q[1]), .en(Enable), .reset(Clear));  // open: Qn, preset
  D_Flip_Flop d_ff_3 (.clk(Clock), .D(I[2]), .Q(Q[2]), .en(Enable), .reset(Clear));  // open: Qn, preset
  D_Flip_Flop d_ff_4 (.clk(Clock), .D(I[3]), .Q(Q[3]), .en(Enable), .reset(Clear));  // open: Qn, preset
  D_Flip_Flop d_ff_5 (.clk(Clock), .D(I[4]), .Q(Q[4]), .en(Enable), .reset(Clear));  // open: Qn, preset
  D_Flip_Flop d_ff_6 (.clk(Clock), .D(I[5]), .Q(Q[5]), .en(Enable), .reset(Clear));  // open: Qn, preset
  D_Flip_Flop d_ff_7 (.clk(Clock), .D(I[6]), .Q(Q[6]), .en(Enable), .reset(Clear));  // open: Qn, preset
  D_Flip_Flop d_ff_8 (.clk(Clock), .D(I[7]), .Q(Q[7]), .en(Enable), .reset(Clear));  // open: Qn, preset
  Hex_Digit_Display hex_digit_display_3 (.value(Q[7:4]));  // open: dp
  Hex_Digit_Display hex_digit_display_4 (.value(Q[3:0]));  // open: dp
endmodule

module CSL (
  input  Carry,
  input  [7:0] Input,
  output [7:0] Output,
  output Carry_2
);


  assign Carry_2 = Input[7];
  assign Output = {Input[6:0], Carry};
endmodule

module CSR (
  input  [7:0] Input,
  input  Carry,
  output [7:0] Output,
  output Carry_2
);


  assign Carry_2 = Input[0];
  assign Output = {Carry, Input[7:1]};
endmodule

module LSL (
  input  [7:0] Input,
  output [7:0] Output,
  output Carry
);


  assign Carry = Input[7];
  assign Output = {Input[6:0], 1'b0};
endmodule

module LSR (
  input  [7:0] Input,
  output [7:0] Output,
  output Carry
);


  assign Carry = Input[0];
  assign Output = {1'b0, Input[7:1]};
endmodule

module ASL (
  input  [7:0] Input,
  output [7:0] Output,
  output Overflow
);

  xor xor_1 (Overflow, Input[6], Input[7]);

  assign Output = {Input[6:0], 1'b0};
endmodule

module ASR (
  input  [7:0] Input,
  output [7:0] Output
);


  assign Output = {{2{Input[7]}}, Input[6:1]};
endmodule

module _8Adder (
  input  [7:0] InputA,
  input  [7:0] InputB,
  input  CIn,
  output [7:0] Output,
  output Overflow,
  output CarryOut
);

  wire n_n_p_out, not_1_out, not_2_out, not_3_out, p_p_n_out;

  Adder adder_1 (.a(InputA), .b(InputB), .out(Output), .cin(CIn), .cout(CarryOut));
  not not_1 (not_1_out, InputA[7]);
  not not_2 (not_2_out, InputB[7]);
  not not_3 (not_3_out, Output[7]);
  and p_p_n (p_p_n_out, not_1_out, not_2_out, Output[7]);
  and n_n_p (n_n_p_out, InputA[7], InputB[7], not_3_out);
  or or_1 (Overflow, p_p_n_out, n_n_p_out);
endmodule

module _8Sub (
  input  [7:0] InputA,
  input  [7:0] InputB,
  output [7:0] Output,
  output Overflow,
  output CarryOut
);

  wire n_p_p_out, not_2_out, not_3_out, not_4_out, p_n_n_out;
  wire [7:0] not_1_out;

  assign not_1_out = ~InputB;  // NOT_Gate not_1, 8 bits wide
  Adder adder_1 (.a(InputA), .b(not_1_out), .out(Output), .cin(1'b1), .cout(CarryOut));
  not not_2 (not_2_out, InputA[7]);
  not not_3 (not_3_out, InputB[7]);
  not not_4 (not_4_out, Output[7]);
  and p_n_n (p_n_n_out, not_2_out, InputB[7], Output[7]);
  and n_p_p (n_p_p_out, InputA[7], not_3_out, not_4_out);
  or or_1 (Overflow, p_n_n_out, n_p_p_out);
endmodule

// Z|C|N|O
module _4R (
  input  [3:0] Input,
  input  Clear,
  input  clock,
  output [3:0] \output 
);

  D_Flip_Flop Z (.clk(clock), .D(Input[3]), .Q(\output [3]), .en(1'b1), .reset(Clear));  // open: Qn, preset
  D_Flip_Flop C (.clk(clock), .D(Input[2]), .Q(\output [2]), .en(1'b1), .reset(Clear));  // open: Qn, preset
  D_Flip_Flop N (.clk(clock), .D(Input[1]), .Q(\output [1]), .en(1'b1), .reset(Clear));  // open: Qn, preset
  D_Flip_Flop O (.clk(clock), .D(Input[0]), .Q(\output [0]), .en(1'b1), .reset(Clear));  // open: Qn, preset
endmodule
