// Logisim project project2.circ as structural Verilog: 7 circuits, main circuit part1a
// 8R
module part1a (
  input  Clock,
  input  [1:0] FunSel,
  input  E,
  input  [7:0] I,
  output [7:0] Q
);

  wire [7:0] adder_1_out, multiplexer_1_out, subtractor_1_out;

  Hex_Digit_Display hex_digit_display_1 (.value(I[3:0]));  // open: dp
  Hex_Digit_Display hex_digit_display_2 (.value(I[7:4]));  // open: dp
  Multiplexer #(.select(2), .width(8)) multiplexer_1 (
    .in0(subtractor_1_out), .in1(adder_1_out), .in2(I), .in3({8{1'b0}}), .out(multiplexer_1_out),
    .sel(FunSel), .en(E));
  _8DFF u_8dff_1 (.I(multiplexer_1_out), .Enable(E), .Clock(Clock), .Q(Q));  // open: Clear
  Hex_Digit_Display hex_digit_display_3 (.value(Q[7:4]));  // open: dp
  Hex_Digit_Display hex_digit_display_4 (.value(Q[3:0]));  // open: dp
  Adder adder_1 (.a(Q), .b(8'h1), .out(adder_1_out));  // open: cin, cout
  Subtractor subtractor_1 (.a(Q), .b(8'h1), .out(subtractor_1_out));  // open: bin, bout
endmodule

// IR
module part1b (
  input  [1:0] FunSel,
  input  Low_High,
  input  Enable,
  input  Clock,
  input  [7:0] Input,
  output [15:0] IRout
);

  wire [15:0] adder_1_out, multiplexer_1_out, multiplexer_2_out, subtractor_1_out;

  Hex_Digit_Display hex_digit_display_1 (.value(Input[7:4]));  // open: dp
  Multiplexer #(.width(16), .enable("false")) multiplexer_1 (
    .in0({Input, IRout[7:0]}), .in1({IRout[15:8], Input}), .out(multiplexer_1_out), .sel(Low_High));
  Hex_Digit_Display hex_digit_display_2 (.value(Input[3:0]));  // open: dp
  Multiplexer #(.select(2), .width(16), .enable("false")) multiplexer_2 (
    .in0(subtractor_1_out), .in1(adder_1_out), .in2(multiplexer_1_out), .in3({16{1'b0}}),
    .out(multiplexer_2_out), .sel(FunSel));
  _8DFF IR_0_7 (.I(multiplexer_2_out[7:0]), .Enable(Enable), .Clock(Clock), .Q(IRout[7:0]));  // open: Clear
  _8DFF IR_8_15 (.I(multiplexer_2_out[15:8]), .Enable(Enable), .Clock(Clock), .Q(IRout[15:8]));  // open: Clear
  Hex_Digit_Display hex_digit_display_3 (.value(IRout[11:8]));  // open: dp
  Hex_Digit_Display hex_digit_display_4 (.value(IRout[15:12]));  // open: dp
  Hex_Digit_Display hex_digit_display_5 (.value(IRout[7:4]));  // open: dp
  Subtractor #(.width(16)) subtractor_1 (.a(IRout), .b(16'h1), .out(subtractor_1_out));  // open: bin, bout
  Adder #(.width(16)) adder_1 (.a(IRout), .b(16'h1), .out(adder_1_out));  // open: cin, cout
  Hex_Digit_Display hex_digit_display_6 (.value(IRout[3:0]));  // open: dp
endmodule

// Register File
module part2a (
  input  Clock,
  input  [7:0] \input ,
  input  [3:0] RegSel,
  input  [2:0] OutASel,
  input  [2:0] OutBSel,
  input  [3:0] TmpSel,
  input  [1:0] FunSel,
  output [7:0] OutA,
  output [7:0] OutB
);

  wire [3:0] not_1_out, not_2_out;
  wire [7:0] R1_q, R2_q, R3_q, R4_q, T1_q, T2_q, T3_q, T4_q;

  assign not_1_out = ~RegSel;  // NOT_Gate not_1, 4 bits wide
  assign not_2_out = ~TmpSel;  // NOT_Gate not_2, 4 bits wide
  Hex_Digit_Display hex_digit_display_1 (.value(\input [3:0]));  // open: dp
  Hex_Digit_Display hex_digit_display_2 (.value(\input [7:4]));  // open: dp
  part1a R1 (.I(\input ), .Clock(Clock), .FunSel(FunSel), .E(not_1_out[3]), .Q(R1_q));
  part1a R2 (.I(\input ), .Clock(Clock), .FunSel(FunSel), .E(not_1_out[2]), .Q(R2_q));
  part1a R3 (.I(\input ), .Clock(Clock), .FunSel(FunSel), .E(not_1_out[1]), .Q(R3_q));
  part1a R4 (.I(\input ), .Clock(Clock), .FunSel(FunSel), .E(not_1_out[0]), .Q(R4_q));
  part1a T1 (.I(\input ), .Clock(Clock), .FunSel(FunSel), .E(not_2_out[3]), .Q(T1_q));
  part1a T2 (.I(\input ), .Clock(Clock), .FunSel(FunSel), .E(not_2_out[2]), .Q(T2_q));
  part1a T3 (.I(\input ), .Clock(Clock), .FunSel(FunSel), .E(not_2_out[1]), .Q(T3_q));
  part1a T4 (.I(\input ), .Clock(Clock), .FunSel(FunSel), .E(not_2_out[0]), .Q(T4_q));
  Multiplexer #(.select(3), .width(8), .enable("false")) multiplexer_1 (
    .in0(R1_q), .in1(R2_q), .in2(R3_q), .in3(R4_q), .in4(T1_q), .in5(T2_q), .in6(T3_q), .in7(T4_q),
    .out(OutA), .sel(OutASel));
  Multiplexer #(.select(3), .width(8), .enable("false")) multiplexer_2 (
    .in0(R1_q), .in1(R2_q), .in2(R3_q), .in3(R4_q), .in4(T1_q), .in5(T2_q), .in6(T3_q), .in7(T4_q),
    .out(OutB), .sel(OutBSel));
  Hex_Digit_Display hex_digit_display_3 (.value(OutA[7:4]));  // open: dp
  Hex_Digit_Display hex_digit_display_4 (.value(OutA[3:0]));  // open: dp
  Hex_Digit_Display hex_digit_display_5 (.value(OutB[3:0]));  // open: dp
  Hex_Digit_Display hex_digit_display_6 (.value(OutB[7:4]));  // open: dp
endmodule

// ARF
module part2b (
  input  Clock,
  input  [7:0] \input ,
  input  [1:0] FunSel,
  input  [1:0] OutCSel,
  input  [1:0] OutDSel,
  input  [2:0] RegSel,
  output [7:0] OutC,
  output [7:0] OutD
);

  wire [2:0] not_1_out;
  wire [7:0] AR_q, PC_q, SP_q;

  Hex_Digit_Display hex_digit_display_1 (.value(\input [7:4]));  // open: dp
  assign not_1_out = ~RegSel;  // NOT_Gate not_1, 3 bits wide
  Hex_Digit_Display hex_digit_display_2 (.value(\input [3:0]));  // open: dp
  part1a PC (.I(\input ), .Clock(Clock), .FunSel(FunSel), .E(not_1_out[2]), .Q(PC_q));
  part1a AR (.I(\input ), .Clock(Clock), .FunSel(FunSel), .E(not_1_out[1]), .Q(AR_q));
  part1a SP (.I(\input ), .Clock(Clock), .FunSel(FunSel), .E(not_1_out[0]), .Q(SP_q));
  Multiplexer #(.select(2), .width(8), .enable("false")) multiplexer_1 (
    .in0(PC_q), .in1(PC_q), .in2(AR_q), .in3(SP_q), .out(OutC), .sel(OutCSel));
  Hex_Digit_Display hex_digit_display_3 (.value(OutC[7:4]));  // open: dp
  Multiplexer #(.select(2), .width(8), .enable("false")) multiplexer_2 (
    .in0(PC_q), .in1(PC_q), .in2(AR_q), .in3(SP_q), .out(OutD), .sel(OutDSel));
  Hex_Digit_Display hex_digit_display_4 (.value(OutC[3:0]));  // open: dp
  Hex_Digit_Display hex_digit_display_5 (.value(OutD[7:4]));  // open: dp
  Hex_Digit_Display hex_digit_display_6 (.value(OutD[3:0]));  // open: dp
endmodule

// ALU
module part3 (
  input  [7:0] A,
  input  Clear,
  input  Clock,
  input  [7:0] B,
  input  [3:0] FunSel,
  output [7:0] OutALU,
  output [3:0] Z_C_N_O
);

  wire and_1_out, asl_1_overflow, csl_1_carry_2, csr_1_carry_2, lsl_1_carry, lsr_1_carry, n8adder_1_carryout,
       n8adder_1_overflow, n8adder_2_carryout, n8adder_2_overflow, n8sub_1_carryout, n8sub_1_overflow,
       not_1_out;
  wire [3:0] multiplexer_3_out;
  wire [7:0] and_2_out, asl_1_output, asr_1_output, csl_1_output, csr_1_output, lsl_1_output, lsr_1_output,
       n8adder_1_output, n8adder_2_output, n8sub_1_output, not_2_out, not_3_out, or_1_out, xor_1_out;

  Hex_Digit_Display hex_digit_display_1 (.value(A[7:4]));  // open: dp
  Hex_Digit_Display hex_digit_display_2 (.value(A[3:0]));  // open: dp
  Hex_Digit_Display hex_digit_display_3 (.value(B[7:4]));  // open: dp
  Hex_Digit_Display hex_digit_display_4 (.value(B[3:0]));  // open: dp
  not not_1 (not_1_out, FunSel[1]);
  and and_1 (and_1_out, FunSel[3], FunSel[2], not_1_out, FunSel[0]);
  _8Adder u_8adder_1 (
    .InputA(A), .InputB(B), .CIn(1'b0), .Output(n8adder_1_output), .Overflow(n8adder_1_overflow),
    .CarryOut(n8adder_1_carryout));
  _8Adder u_8adder_2 (
    .InputA(A), .InputB(B), .CIn(Z_C_N_O[2]), .Output(n8adder_2_output), .Overflow(n8adder_2_overflow),
    .CarryOut(n8adder_2_carryout));
  _8Sub u_8sub_1 (
    .InputA(A), .InputB(B), .Output(n8sub_1_output), .Overflow(n8sub_1_overflow), .CarryOut(n8sub_1_carryout));
  assign and_2_out = A & B;  // AND_Gate and_2, 8 bits wide
  assign or_1_out = A | B;  // OR_Gate or_1, 8 bits wide
  assign xor_1_out = A ^ B;  // XOR_Gate xor_1, 8 bits wide
  LSL lsl_1 (.Input(A), .Output(lsl_1_output), .Carry(lsl_1_carry));
  LSR lsr_1 (.Input(A), .Output(lsr_1_output), .Carry(lsr_1_carry));
  ASL asl_1 (.Input(A), .Output(asl_1_output), .Overflow(asl_1_overflow));
  ASR asr_1 (.Input(A), .Output(asr_1_output));
  CSL csl_1 (.Carry(Z_C_N_O[2]), .Input(A), .Output(csl_1_output), .Carry_2(csl_1_carry_2));
  CSR csr_1 (.Input(A), .Carry(Z_C_N_O[2]), .Output(csr_1_output), .Carry_2(csr_1_carry_2));
  assign not_2_out = ~A;  // NOT_Gate not_2, 8 bits wide
  assign not_3_out = ~B;  // NOT_Gate not_3, 8 bits wide
  Multiplexer #(.select(4), .width(8), .enable("false")) multiplexer_1 (
    .in0(A), .in1(B), .in2(not_2_out), .in3(not_3_out), .in4(n8adder_1_output), .in5(n8adder_2_output),
    .in6(n8sub_1_output), .in7(and_2_out), .in8(or_1_out), .in9(xor_1_out), .in10(lsl_1_output),
    .in11(lsr_1_output), .in12(asl_1_output), .in13(asr_1_output), .in14(csl_1_output), .in15(csr_1_output),
    .out(OutALU), .sel(FunSel));
  Multiplexer #(.select(4), .enable("false")) multiplexer_2 (
    .in0(Z_C_N_O[2]), .in1(Z_C_N_O[2]), .in2(Z_C_N_O[2]), .in3(Z_C_N_O[2]), .in4(n8adder_1_carryout),
    .in5(n8adder_2_carryout), .in6(n8sub_1_carryout), .in7(Z_C_N_O[2]), .in8(Z_C_N_O[2]), .in9(Z_C_N_O[2]),
    .in10(lsl_1_carry), .in11(lsr_1_carry), .in12(Z_C_N_O[2]), .in13(Z_C_N_O[2]), .in14(csl_1_carry_2),
    .in15(csr_1_carry_2), .out(multiplexer_3_out[2]), .sel(FunSel));
  Multiplexer #(.select(4), .enable("false")) multiplexer_3 (
    .in0(Z_C_N_O[0]), .in1(Z_C_N_O[0]), .in2(Z_C_N_O[0]), .in3(Z_C_N_O[0]), .in4(n8adder_1_overflow),
    .in5(n8adder_2_overflow), .in6(n8sub_1_overflow), .in7(Z_C_N_O[0]), .in8(Z_C_N_O[0]), .in9(Z_C_N_O[0]),
    .in10(Z_C_N_O[0]), .in11(Z_C_N_O[0]), .in12(asl_1_overflow), .in13(Z_C_N_O[0]), .in14(Z_C_N_O[0]),
    .in15(Z_C_N_O[0]), .out(multiplexer_3_out[0]), .sel(FunSel));
  nor nor_1 (multiplexer_3_out[3], OutALU[0], OutALU[1], OutALU[2], OutALU[3], OutALU[4], OutALU[5], OutALU[6], OutALU[7]);
  Multiplexer #(.enable("false")) multiplexer_4 (
    .in0(OutALU[7]), .in1(Z_C_N_O[1]), .out(multiplexer_3_out[1]), .sel(and_1_out));
  _4R u_4r_1 (.Input(multiplexer_3_out), .clock(Clock), .Clear(Clear), .\output (Z_C_N_O));
  Hex_Digit_Display hex_digit_display_5 (.value(OutALU[7:4]));  // open: dp
  Hex_Digit_Display hex_digit_display_6 (.value(OutALU[3:0]));  // open: dp

  // Notes on the sheet:
  //   A
  //   B
endmodule

module part4 (
  input  in_1,
  output [3:0] Z_C_N_O,
  output [7:0] out_3,
  output [7:0] out_4,
  output [7:0] out_5
);

  wire Enable, L_H, Load, Read;
  wire [1:0] FunSelA, FunSelB, FunSelC, MuxASel, MuxBSel, OutCSel, OutDSel;
  wire [2:0] OutASel, OutBSel, RegSelB;
  wire [3:0] FunSelALU, RegSelA, TmpSelA;
  wire [7:0] multiplexer_1_out, multiplexer_2_out, part2a_1_outa, part2a_1_outb, part2b_1_outc,
       part2b_1_outd, ram_1_data;

  Multiplexer #(.select(2), .width(8), .enable("false")) multiplexer_1 (
    .in0(out_3), .in1(ram_1_data), .in2(out_4), .in3(part2b_1_outc), .out(multiplexer_1_out), .sel(MuxASel));
  Multiplexer #(.select(2), .width(8), .enable("false")) multiplexer_2 (
    .in0(out_3), .in1(ram_1_data), .in2(out_4), .in3(part2b_1_outc), .out(multiplexer_2_out), .sel(MuxBSel));
  part1b part1b_1 (
    .Input(ram_1_data), .FunSel(FunSelC), .Low_High(L_H), .Enable(Enable), .Clock(in_1),
    .IRout({out_5, out_4}));
  part2a part2a_1 (
    .\input (multiplexer_1_out), .RegSel(RegSelA), .TmpSel(TmpSelA), .FunSel(FunSelA), .Clock(in_1),
    .OutASel(OutASel), .OutBSel(OutBSel), .OutA(part2a_1_outa), .OutB(part2a_1_outb));
  Conunit conunit_1 (
    .Clock(in_1), .Z(Z_C_N_O[3]), ._16Bit_Data({out_5, out_4}), .RegSelB(RegSelB), .OutBSel(OutBSel),
    .OutASel(OutASel), .OutDSel(OutDSel), .RegSelA(RegSelA), .FunSelA(FunSelA), .FunSelB(FunSelB),
    .MuxASel(MuxASel), .TmpSelA(TmpSelA), .FunSelALU(FunSelALU), .FunselC(FunSelC), .OutCSel(OutCSel),
    .MuxBSel(MuxBSel), .L_H(L_H), .Enable(Enable), .Load(Load), .Read(Read));
  part2b part2b_1 (
    .\input (multiplexer_2_out), .Clock(in_1), .RegSel(RegSelB), .FunSel(FunSelB), .OutCSel(OutCSel),
    .OutDSel(OutDSel), .OutC(part2b_1_outc), .OutD(part2b_1_outd));
  part3 part3_1 (
    .A(part2a_1_outa), .B(part2a_1_outb), .FunSel(FunSelALU), .Z_C_N_O(Z_C_N_O), .Clock(in_1), .OutALU(out_3));  // open: Clear
  RAM #(.bus("separate")) ram_1 (
    .addr(part2b_1_outd), .din(out_3), .data(ram_1_data), .str(Load), .clk(in_1), .ld(Read));  // open: sel, clr

  // Other names for the same wires on the sheet: Z = Z_C_N_O[3]
endmodule

module Conunit (
  input  Clock,
  input  Z,
  input  [15:0] _16Bit_Data,
  output [2:0] RegSelB,
  output [2:0] OutBSel,
  output [2:0] OutASel,
  output [1:0] OutDSel,
  output [3:0] RegSelA,
  output [1:0] FunSelA,
  output [1:0] FunSelB,
  output [1:0] MuxASel,
  output [3:0] TmpSelA,
  output [3:0] FunSelALU,
  output [1:0] FunselC,
  output [1:0] OutCSel,
  output [1:0] MuxBSel,
  output L_H,
  output Enable,
  output Load,
  output Read
);

  wire and_2_out, and_3_out, and_4_out, and_5_out, and_6_out, and_7_out, and_8_out, and_9_out, and_10_out,
       and_11_out, and_12_out, and_13_out, and_14_out, and_15_out, and_16_out, and_17_out, and_18_out,
       and_19_out, and_20_out, and_21_out, and_30_out, and_31_out, and_32_out, and_33_out, and_34_out,
       and_35_out, and_36_out, and_37_out, and_38_out, and_39_out, and_40_out, and_41_out, and_42_out,
       and_43_out, and_44_out, and_45_out, and_46_out, and_47_out, and_48_out, and_49_out, and_50_out,
       and_51_out, and_52_out, and_53_out, and_54_out, and_55_out, and_56_out, and_57_out, and_58_out,
       and_59_out, and_60_out, and_61_out, and_62_out, and_63_out, and_64_out, and_65_out, and_66_out,
       and_67_out, and_68_out, and_69_out, and_70_out, and_71_out, and_72_out, and_73_out, and_74_out,
       and_75_out, and_76_out, and_77_out, and_78_out, and_79_out, and_80_out, and_81_out, and_82_out,
       and_83_out, and_84_out, and_85_out, and_86_out, and_87_out, and_88_out, and_89_out, and_90_out,
       and_91_out, and_92_out, and_93_out, and_94_out, and_95_out, and_96_out, and_97_out, and_98_out,
       and_99_out, and_100_out, and_101_out, and_102_out, and_103_out, and_104_out, and_105_out, and_106_out,
       and_107_out, and_108_out, and_109_out, and_110_out, and_111_out, and_112_out, and_113_out,
       and_114_out, and_115_out, and_116_out, and_117_out, and_118_out, and_119_out, and_120_out,
       and_121_out, and_122_out, and_123_out, and_124_out, and_125_out, and_126_out, and_127_out,
       and_128_out, and_129_out, and_130_out, and_131_out, and_132_out, and_133_out, and_134_out,
       and_135_out, and_136_out, and_137_out, and_138_out, and_139_out, and_140_out, and_141_out,
       and_142_out, and_143_out, and_144_out, and_145_out, and_146_out, and_147_out, and_148_out,
       and_149_out, and_150_out, and_151_out, and_152_out, and_153_out, and_154_out, and_155_out,
       and_156_out, and_157_out, and_158_out, and_159_out, and_160_out, and_161_out, and_162_out,
       and_163_out, and_164_out, and_165_out, and_166_out, and_167_out, and_168_out, and_169_out,
       and_170_out, and_171_out, and_172_out, and_173_out, and_174_out, and_175_out, and_176_out,
       and_177_out, and_178_out, and_179_out, and_180_out, and_181_out, and_182_out, and_183_out,
       and_184_out, and_185_out, and_186_out, and_187_out, and_188_out, and_189_out, and_190_out,
       and_191_out, and_192_out, and_193_out, and_194_out, and_195_out, and_196_out, and_197_out,
       and_198_out, and_199_out, and_200_out, and_201_out, and_202_out, and_203_out, and_204_out,
       and_205_out, and_206_out, and_207_out, and_208_out, and_209_out, and_210_out, and_211_out,
       and_212_out, and_213_out, and_214_out, and_215_out, and_216_out, and_217_out, and_218_out,
       and_219_out, and_220_out, and_221_out, and_222_out, and_223_out, and_224_out, and_225_out,
       ARF_ARF_ARF, ARF_ARF_Rx, ARF_Rx_ARF, ARF_Rx_Rx, Finish, not_1_out, not_2_out, not_3_out, not_4_out,
       not_5_out, not_6_out, not_7_out, not_8_out, not_9_out, not_10_out, not_11_out, not_12_out, not_13_out,
       not_14_out, not_15_out, not_16_out, not_17_out, not_18_out, not_19_out, not_20_out, not_21_out,
       not_22_out, not_23_out, not_24_out, not_25_out, not_26_out, not_27_out, not_28_out, not_29_out,
       not_30_out, not_31_out, not_32_out, not_33_out, not_34_out, not_35_out, not_36_out, not_37_out,
       not_38_out, not_39_out, not_40_out, not_41_out, not_42_out, not_43_out, not_44_out, not_45_out,
       not_46_out, not_47_out, not_48_out, not_49_out, not_50_out, not_51_out, not_52_out, not_53_out,
       not_54_out, not_55_out, not_56_out, not_57_out, not_58_out, not_59_out, not_60_out, not_61_out,
       not_62_out, not_63_out, not_64_out, not_65_out, not_66_out, not_67_out, not_68_out, not_69_out,
       not_70_out, not_71_out, not_72_out, not_73_out, not_74_out, not_75_out, not_76_out, not_77_out,
       not_78_out, not_79_out, not_80_out, not_81_out, not_82_out, not_83_out, not_84_out, not_85_out,
       not_86_out, not_87_out, not_88_out, not_89_out, not_90_out, not_91_out, not_92_out, not_93_out,
       not_94_out, not_95_out, not_96_out, not_97_out, not_98_out, not_99_out, not_100_out, not_101_out,
       not_102_out, not_103_out, not_104_out, not_105_out, not_106_out, not_107_out, not_108_out,
       not_109_out, OP0, OP1, OP2, OP3, OP4, OP4_5_7_8, OP5, OP6, OP6_9_10, OP7, OP8, OP9, OP10, OP11, OP12,
       OP13, OP13_14, OP14, OP15, or_2_out, or_3_out, or_4_out, or_5_out, or_6_out, or_8_out, or_9_out,
       or_11_out, or_15_out, or_16_out, or_17_out, or_18_out, or_19_out, or_20_out, or_21_out, or_22_out,
       or_23_out, or_24_out, or_25_out, or_26_out, or_27_out, or_28_out, or_29_out, or_30_out, or_31_out,
       or_32_out, or_33_out, or_34_out, or_35_out, or_36_out, or_37_out, or_38_out, or_39_out, or_40_out,
       or_41_out, or_42_out, or_43_out, or_44_out, or_45_out, or_46_out, or_47_out, or_48_out, or_49_out,
       or_50_out, or_51_out, or_52_out, or_53_out, or_54_out, or_55_out, or_56_out, or_57_out, or_58_out,
       or_59_out, or_60_out, or_61_out, or_62_out, or_63_out, or_64_out, or_65_out, or_66_out, or_67_out,
       or_68_out, or_69_out, or_70_out, or_71_out, or_72_out, or_73_out, or_74_out, or_75_out, or_76_out,
       or_77_out, or_78_out, or_79_out, or_80_out, or_81_out, or_82_out, or_83_out, or_84_out, or_85_out,
       or_86_out, or_87_out, or_88_out, or_89_out, or_90_out, or_91_out, or_92_out, or_93_out, or_94_out,
       or_95_out, or_96_out, or_97_out, or_98_out, or_99_out, or_100_out, or_101_out, or_102_out, or_103_out,
       or_104_out, or_105_out, or_106_out, or_107_out, or_108_out, or_109_out, or_110_out, or_111_out,
       or_112_out, or_113_out, or_114_out, or_115_out, or_116_out, or_117_out, or_118_out, Rx_ARF_ARF,
       Rx_ARF_Rx, Rx_Rx_ARF, Rx_Rx_Rx, T0, T1, T2, T3, T4, T5, xnor_1_out, xnor_2_out, xnor_3_out, xnor_4_out;
  wire [2:0] ARF_RegSel, ARF_RegSel_1, counter_1_q;
  wire [3:0] New_RegSel, New_RegSel_1, New_TmpSel, New_TmpSel_2, SRCREG1, SRCREG2;

  and and_1 (L_H, T0, not_1_out);
  not not_1 (not_1_out, T1);
  or or_1 (Enable, T0, T1);
  not not_2 (not_2_out, OP8);
  not not_3 (not_3_out, OP8);
  not not_4 (not_4_out, _16Bit_Data[10]);
  assign SRCREG1 = OP8 ? _16Bit_Data[3:0] : 4'bz;  // Controlled_Buffer controlled_buffer_1
  assign SRCREG2 = not_2_out ? _16Bit_Data[3:0] : 4'bz;  // Controlled_Buffer controlled_buffer_2
  assign SRCREG2 = OP8 ? _16Bit_Data[7:4] : 4'bz;  // Controlled_Buffer controlled_buffer_3
  assign SRCREG1 = not_3_out ? _16Bit_Data[7:4] : 4'bz;  // Controlled_Buffer controlled_buffer_4
  and and_2 (and_2_out, OP0, T3);
  and and_3 (and_3_out, OP1, T3);
  and and_4 (and_4_out, OP2, T3);
  and and_5 (and_5_out, OP3, T3);
  and and_6 (and_6_out, _16Bit_Data[10], SRCREG1[2]);
  and and_7 (and_7_out, not_4_out, SRCREG1[2]);
  or or_2 (or_2_out, and_6_out, and_7_out);
  or or_3 (or_3_out, Rx_Rx_Rx, ARF_Rx_Rx);
  or or_4 (or_4_out, Rx_Rx_ARF, Rx_ARF_Rx, ARF_ARF_Rx, ARF_Rx_ARF);
  or or_5 (or_5_out, OP11, OP12);
  xnor xnor_1 (xnor_1_out, _16Bit_Data[8], SRCREG1[0]);
  xnor xnor_2 (xnor_2_out, _16Bit_Data[9], SRCREG1[1]);
  xnor xnor_3 (xnor_3_out, _16Bit_Data[10], SRCREG1[2]);
  xnor xnor_4 (xnor_4_out, _16Bit_Data[11], SRCREG1[3]);
  Decoder #(.select(3), .enable("false")) decoder_1 (
    .out0(T0), .out1(T1), .out2(T2), .out3(T3), .out4(T4), .out5(T5), .sel(counter_1_q));  // open: out6, out7
  Counter #(.width(3), .max('h7)) counter_1 (
    .count(1'b1), .Q(counter_1_q), .clk(Clock), .clr(Finish));  // open: load, D, carry
  and and_8 (and_8_out, OP6_9_10, T3, or_2_out);
  and and_9 (and_9_out, OP6_9_10, T4);
  and and_10 (and_10_out, OP13_14, T5);
  and and_11 (and_11_out, OP4_5_7_8, T3, or_3_out);
  and and_12 (and_12_out, OP4_5_7_8, T4, or_4_out);
  and and_13 (and_13_out, OP4_5_7_8, T5);
  and and_14 (and_14_out, or_5_out, T4);
  Decoder #(.select(4), .enable("false")) decoder_2 (
    .out0(OP0), .out1(OP1), .out2(OP2), .out3(OP3), .out4(OP4), .out5(OP5), .out6(OP6), .out7(OP7),
    .out8(OP8), .out9(OP9), .out10(OP10), .out11(OP11), .out12(OP12), .out13(OP13), .out14(OP14),
    .out15(OP15), .sel(_16Bit_Data[15:12]));
  Multiplexer #(.select(2), .width(4), .enable("false")) multiplexer_1 (
    .in0(4'b0111), .in1(4'b1011), .in2(4'b1101), .in3(4'b1110), .out(New_RegSel), .sel(_16Bit_Data[9:8]));
  and and_15 (and_15_out, xnor_1_out, xnor_2_out, xnor_3_out, xnor_4_out);
  or or_6 (or_6_out, OP13, OP14);
  Multiplexer #(.select(2), .width(4), .enable("false")) multiplexer_2 (
    .in0(4'b0111), .in1(4'b1011), .in2(4'b1101), .in3(4'b1110), .out(New_TmpSel_2), .sel(SRCREG2[1:0]));
  or or_7 (Finish, and_2_out, and_3_out, and_4_out, and_5_out, or_8_out);
  and and_16 (and_16_out, and_15_out, or_6_out, T4);
  or or_8 (or_8_out, and_8_out, and_9_out, and_10_out, and_11_out, and_12_out, and_13_out, and_14_out, and_16_out, and_17_out);
  and and_17 (and_17_out, OP15, T3);
  Multiplexer #(.select(2), .width(4), .enable("false")) multiplexer_3 (
    .in0(4'b0111), .in1(4'b1011), .in2(4'b1101), .in3(4'b1110), .out(New_RegSel_1), .sel(_16Bit_Data[9:8]));
  Multiplexer #(.select(2), .width(4), .enable("false")) multiplexer_4 (
    .in0(4'b0111), .in1(4'b1011), .in2(4'b1101), .in3(4'b1110), .out(New_TmpSel), .sel(SRCREG1[1:0]));
  not not_5 (not_5_out, _16Bit_Data[10]);
  not not_6 (not_6_out, _16Bit_Data[10]);
  or or_9 (or_9_out, T0, T1);
  and and_18 (and_18_out, OP1, T2, not_5_out);
  and and_19 (and_19_out, OP11, T3);
  or or_10 (OP6_9_10, OP6, OP9, OP10);
  and and_20 (and_20_out, OP2, not_6_out, T2);
  and and_21 (and_21_out, OP12, T2);
  Multiplexer #(.select(2), .width(3), .enable("false")) multiplexer_5 (
    .in0(3'b011), .in1(3'b011), .in2(3'b101), .in3(3'b110), .out(ARF_RegSel), .sel(_16Bit_Data[9:8]));
  Multiplexer #(.select(2), .width(3), .enable("false")) multiplexer_6 (
    .in0(3'b011), .in1(3'b011), .in2(3'b101), .in3(3'b110), .out(ARF_RegSel_1), .sel(SRCREG1[1:0]));
  not not_7 (not_7_out, _16Bit_Data[10]);
  not not_8 (not_8_out, SRCREG2[2]);
  not not_9 (not_9_out, _16Bit_Data[10]);
  assign Read = or_11_out ? 1'b1 : 1'bz;  // Controlled_Buffer controlled_buffer_5
  or or_11 (or_11_out, or_9_out, and_18_out, and_19_out);
  or or_12 (OP13_14, OP13, OP14);
  not not_10 (not_10_out, SRCREG2[2]);
  not not_11 (not_11_out, SRCREG1[2]);
  not not_12 (not_12_out, SRCREG1[2]);
  not not_13 (not_13_out, SRCREG2[2]);
  not not_14 (not_14_out, _16Bit_Data[10]);
  not not_15 (not_15_out, SRCREG1[2]);
  not not_16 (not_16_out, SRCREG2[2]);
  not not_17 (not_17_out, _16Bit_Data[10]);
  not not_18 (not_18_out, SRCREG1[2]);
  and and_22 (ARF_Rx_ARF, not_7_out, SRCREG1[2], not_8_out);
  and and_23 (ARF_Rx_Rx, not_9_out, SRCREG1[2], SRCREG2[2]);
  or or_13 (Load, and_20_out, and_21_out);
  or or_14 (OP4_5_7_8, OP4, OP5, OP7, OP8);
  and and_24 (Rx_Rx_Rx, _16Bit_Data[10], SRCREG1[2], SRCREG2[2]);
  and and_25 (Rx_Rx_ARF, _16Bit_Data[10], SRCREG1[2], not_10_out);
  and and_26 (Rx_ARF_Rx, _16Bit_Data[10], not_11_out, SRCREG2[2]);
  and and_27 (Rx_ARF_ARF, _16Bit_Data[10], not_12_out, not_13_out);
  and and_28 (ARF_ARF_ARF, not_14_out, not_15_out, not_16_out);
  and and_29 (ARF_ARF_Rx, not_17_out, not_18_out, SRCREG2[2]);
  not not_19 (not_19_out, SRCREG1[2]);
  not not_20 (not_20_out, SRCREG1[2]);
  not not_21 (not_21_out, SRCREG1[2]);
  and and_30 (and_30_out, _16Bit_Data[10], SRCREG1[2]);
  or or_15 (or_15_out, and_30_out, and_31_out);
  and and_31 (and_31_out, _16Bit_Data[10], not_19_out);
  and and_32 (and_32_out, _16Bit_Data[10], SRCREG1[2]);
  not not_22 (not_22_out, _16Bit_Data[10]);
  and and_33 (and_33_out, OP13_14, T3, or_15_out);
  and and_34 (and_34_out, OP4_5_7_8, T3, or_16_out);
  or or_16 (or_16_out, Rx_Rx_ARF, Rx_ARF_Rx);
  and and_35 (and_35_out, OP4_5_7_8, T4, Rx_ARF_ARF);
  and and_36 (and_36_out, OP11, T3);
  or or_17 (or_17_out, T2, T4);
  or or_18 (or_18_out, and_32_out, and_37_out);
  and and_37 (and_37_out, not_22_out, SRCREG1[2]);
  and and_38 (and_38_out, OP3, T2, _16Bit_Data[10], SRCREG1[2]);
  and and_39 (and_39_out, OP3, T2, _16Bit_Data[10], not_20_out);
  and and_40 (and_40_out, OP6_9_10, T2, _16Bit_Data[10], SRCREG1[2]);
  and and_41 (and_41_out, OP6_9_10, T3, _16Bit_Data[10], not_21_out);
  and and_42 (and_42_out, OP4_5_7_8, T2, Rx_Rx_Rx);
  and and_43 (and_43_out, OP13_14, or_17_out, or_18_out);
  and and_44 (and_44_out, OP1, T2);
  assign RegSelA = and_43_out ? New_TmpSel : 4'bz;  // Controlled_Buffer controlled_buffer_6
  assign RegSelA = and_44_out ? New_RegSel : 4'bz;  // Controlled_Buffer controlled_buffer_7
  assign RegSelA = or_19_out ? New_RegSel_1 : 4'bz;  // Controlled_Buffer controlled_buffer_8
  or or_19 (or_19_out, and_38_out, and_39_out, and_40_out, and_41_out, and_33_out, and_42_out, and_34_out, and_35_out, and_36_out);
  not not_23 (not_23_out, _16Bit_Data[10]);
  not not_24 (not_24_out, Z);
  not not_25 (not_25_out, _16Bit_Data[10]);
  not not_26 (not_26_out, SRCREG1[2]);
  not not_27 (not_27_out, _16Bit_Data[10]);
  not not_28 (not_28_out, _16Bit_Data[10]);
  and and_45 (and_45_out, not_28_out, SRCREG1[2]);
  and and_46 (and_46_out, not_23_out, not_29_out);
  not not_29 (not_29_out, SRCREG1[2]);
  not not_30 (not_30_out, _16Bit_Data[10]);
  and and_47 (and_47_out, not_30_out, SRCREG1[2]);
  not not_31 (not_31_out, _16Bit_Data[10]);
  and and_48 (and_48_out, not_31_out, not_32_out);
  not not_32 (not_32_out, SRCREG1[2]);
  not not_33 (not_33_out, SRCREG1[2]);
  not not_34 (not_34_out, _16Bit_Data[10]);
  not not_35 (not_35_out, SRCREG1[2]);
  or or_20 (or_20_out, and_47_out, and_48_out);
  and and_49 (and_49_out, OP4_5_7_8, T2, ARF_Rx_Rx);
  or or_21 (or_21_out, ARF_ARF_Rx, ARF_Rx_ARF);
  and and_50 (and_50_out, OP4_5_7_8, T4, ARF_ARF_ARF);
  or or_22 (or_22_out, T2, T4);
  and and_51 (and_51_out, _16Bit_Data[10], not_33_out);
  or or_23 (or_23_out, and_51_out, and_52_out);
  and and_52 (and_52_out, not_34_out, not_35_out);
  and and_53 (and_53_out, OP0, _16Bit_Data[10], T2);
  and and_54 (and_54_out, OP15, _16Bit_Data[10], T2, not_24_out);
  and and_55 (and_55_out, OP3, T2, not_25_out, not_26_out);
  and and_56 (and_56_out, OP3, T2, not_27_out, SRCREG1[2]);
  and and_57 (and_57_out, OP6_9_10, T2, and_45_out);
  and and_58 (and_58_out, OP6_9_10, T3, and_46_out);
  and and_59 (and_59_out, OP13_14, T3, or_20_out);
  and and_60 (and_60_out, OP4_5_7_8, T3, or_21_out);
  and and_61 (and_61_out, OP13_14, or_22_out, or_23_out);
  and and_62 (and_62_out, OP11, T2);
  and and_63 (and_63_out, OP12, T3);
  assign RegSelB = and_61_out ? ARF_RegSel_1 : 3'bz;  // Controlled_Buffer controlled_buffer_9
  assign RegSelB = or_24_out ? 3'b110 : 3'bz;  // Controlled_Buffer controlled_buffer_10
  or or_24 (or_24_out, and_62_out, and_63_out);
  assign RegSelB = or_25_out ? 3'b011 : 3'bz;  // Controlled_Buffer controlled_buffer_11
  or or_25 (or_25_out, and_53_out, T0, T1, and_54_out);
  assign RegSelB = or_26_out ? ARF_RegSel : 3'bz;  // Controlled_Buffer controlled_buffer_12
  or or_26 (or_26_out, and_55_out, and_56_out, and_57_out, and_58_out, and_59_out, and_49_out, and_60_out, and_50_out);
  and and_64 (and_64_out, OP4_5_7_8, T3, or_27_out);
  or or_27 (or_27_out, Rx_Rx_ARF, Rx_ARF_Rx);
  not not_36 (not_36_out, _16Bit_Data[10]);
  not not_37 (not_37_out, _16Bit_Data[10]);
  and and_65 (and_65_out, _16Bit_Data[10], not_38_out);
  not not_38 (not_38_out, SRCREG1[2]);
  not not_39 (not_39_out, _16Bit_Data[10]);
  not not_40 (not_40_out, SRCREG1[2]);
  not not_41 (not_41_out, _16Bit_Data[10]);
  and and_66 (and_66_out, _16Bit_Data[10], SRCREG1[2]);
  or or_28 (or_28_out, and_66_out, and_67_out);
  and and_67 (and_67_out, not_36_out, SRCREG1[2]);
  and and_68 (and_68_out, _16Bit_Data[10], SRCREG1[2]);
  not not_42 (not_42_out, _16Bit_Data[10]);
  and and_69 (and_69_out, _16Bit_Data[10], SRCREG1[2]);
  or or_29 (or_29_out, and_69_out, and_70_out);
  and and_70 (and_70_out, not_37_out, SRCREG1[2]);
  not not_43 (not_43_out, SRCREG1[2]);
  or or_30 (or_30_out, and_65_out, and_71_out);
  and and_71 (and_71_out, not_39_out, not_40_out);
  and and_72 (and_72_out, _16Bit_Data[10], SRCREG1[2]);
  and and_73 (and_73_out, _16Bit_Data[10], not_44_out);
  not not_44 (not_44_out, SRCREG1[2]);
  or or_31 (or_31_out, ARF_Rx_ARF, Rx_Rx_Rx, Rx_Rx_ARF, Rx_ARF_Rx, Rx_ARF_ARF, ARF_ARF_ARF, ARF_ARF_Rx);
  and and_74 (and_74_out, _16Bit_Data[10], SRCREG1[2]);
  and and_75 (and_75_out, not_41_out, SRCREG1[2]);
  or or_32 (or_32_out, and_68_out, and_76_out);
  and and_76 (and_76_out, not_42_out, SRCREG1[2]);
  and and_77 (and_77_out, OP13, T4, or_29_out);
  not not_45 (not_45_out, SRCREG1[2]);
  or or_33 (or_33_out, and_72_out, and_73_out);
  and and_78 (and_78_out, OP4_5_7_8, T2, or_31_out);
  and and_79 (and_79_out, OP4_5_7_8, T4, Rx_ARF_ARF);
  and and_80 (and_80_out, OP13, T2, or_34_out);
  or or_34 (or_34_out, and_74_out, and_75_out);
  and and_81 (and_81_out, OP14, T4, or_28_out);
  and and_82 (and_82_out, OP14, T2, or_32_out);
  and and_83 (and_83_out, OP1, T2);
  and and_84 (and_84_out, OP3, T2, _16Bit_Data[10], SRCREG1[2]);
  and and_85 (and_85_out, OP3, T2, _16Bit_Data[10], not_45_out);
  and and_86 (and_86_out, OP6_9_10, T2, _16Bit_Data[10], SRCREG1[2]);
  and and_87 (and_87_out, OP6_9_10, T2, _16Bit_Data[10], not_43_out);
  and and_88 (and_88_out, OP6_9_10, T2, or_30_out);
  and and_89 (and_89_out, OP13_14, T3, or_33_out);
  or or_35 (or_35_out, Rx_ARF_ARF, ARF_ARF_ARF);
  and and_90 (and_90_out, OP4_5_7_8, T3, or_35_out);
  and and_91 (and_91_out, OP11, T3);
  assign FunSelA = or_36_out ? 2'b01 : 2'bz;  // Controlled_Buffer controlled_buffer_13
  or or_36 (or_36_out, and_80_out, and_81_out);
  assign FunSelA = or_37_out ? 2'b00 : 2'bz;  // Controlled_Buffer controlled_buffer_14
  or or_37 (or_37_out, and_82_out, and_77_out);
  assign FunSelA = or_38_out ? 2'b10 : 2'bz;  // Controlled_Buffer controlled_buffer_15
  or or_38 (or_38_out, and_83_out, and_84_out, and_85_out, and_86_out, and_87_out, and_88_out, and_89_out, and_78_out, and_90_out, and_64_out, and_79_out, and_91_out);
  not not_46 (not_46_out, SRCREG1[2]);
  not not_47 (not_47_out, _16Bit_Data[10]);
  not not_48 (not_48_out, SRCREG1[2]);
  and and_92 (and_92_out, _16Bit_Data[10], not_49_out);
  not not_49 (not_49_out, SRCREG1[2]);
  not not_50 (not_50_out, _16Bit_Data[10]);
  and and_93 (and_93_out, not_50_out, not_51_out);
  not not_51 (not_51_out, SRCREG1[2]);
  not not_52 (not_52_out, Z);
  not not_53 (not_53_out, SRCREG1[2]);
  not not_54 (not_54_out, _16Bit_Data[10]);
  not not_55 (not_55_out, SRCREG1[2]);
  not not_56 (not_56_out, SRCREG1[2]);
  not not_57 (not_57_out, _16Bit_Data[10]);
  not not_58 (not_58_out, SRCREG1[2]);
  and and_94 (and_94_out, _16Bit_Data[10], not_46_out);
  and and_95 (and_95_out, not_47_out, not_48_out);
  or or_39 (or_39_out, and_92_out, and_93_out);
  not not_59 (not_59_out, _16Bit_Data[10]);
  not not_60 (not_60_out, SRCREG1[2]);
  not not_61 (not_61_out, _16Bit_Data[10]);
  not not_62 (not_62_out, _16Bit_Data[10]);
  not not_63 (not_63_out, _16Bit_Data[10]);
  not not_64 (not_64_out, SRCREG1[2]);
  not not_65 (not_65_out, _16Bit_Data[10]);
  not not_66 (not_66_out, _16Bit_Data[10]);
  not not_67 (not_67_out, SRCREG1[2]);
  and and_96 (and_96_out, _16Bit_Data[10], not_53_out);
  and and_97 (and_97_out, not_54_out, not_55_out);
  and and_98 (and_98_out, _16Bit_Data[10], not_56_out);
  and and_99 (and_99_out, not_57_out, not_58_out);
  and and_100 (and_100_out, OP14, T2, or_40_out);
  or or_40 (or_40_out, and_94_out, and_95_out);
  and and_101 (and_101_out, OP13, T4, or_39_out);
  and and_102 (and_102_out, OP12, T3);
  and and_103 (and_103_out, OP15, _16Bit_Data[10], T2, not_52_out);
  and and_104 (and_104_out, not_62_out, SRCREG1[2]);
  and and_105 (and_105_out, not_63_out, not_64_out);
  and and_106 (and_106_out, not_65_out, SRCREG1[2]);
  and and_107 (and_107_out, not_66_out, not_67_out);
  and and_108 (and_108_out, OP4_5_7_8, T3, or_41_out);
  or or_41 (or_41_out, ARF_ARF_Rx, ARF_Rx_ARF);
  and and_109 (and_109_out, OP4_5_7_8, T4, ARF_ARF_ARF);
  or or_42 (or_42_out, T0, T1);
  or or_43 (or_43_out, and_96_out, and_97_out);
  or or_44 (or_44_out, and_98_out, and_99_out);
  and and_110 (and_110_out, OP0, _16Bit_Data[10], T2);
  and and_111 (and_111_out, OP3, T2, not_59_out, not_60_out);
  and and_112 (and_112_out, OP3, T2, not_61_out, SRCREG1[2]);
  or or_45 (or_45_out, and_106_out, and_107_out);
  and and_113 (and_113_out, OP4_5_7_8, T2, ARF_Rx_Rx);
  and and_114 (and_114_out, OP13, T2, or_43_out);
  and and_115 (and_115_out, OP14, T4, or_44_out);
  and and_116 (and_116_out, OP11, T2);
  and and_117 (and_117_out, OP6_9_10, T2, and_104_out);
  and and_118 (and_118_out, OP6_9_10, T3, and_105_out);
  and and_119 (and_119_out, OP13_14, T3, or_45_out);
  or or_46 (or_46_out, or_42_out, and_114_out, and_115_out, and_116_out);
  or or_47 (or_47_out, and_100_out, and_101_out, and_102_out);
  assign FunSelB = or_46_out ? 2'b01 : 2'bz;  // Controlled_Buffer controlled_buffer_16
  assign FunSelB = or_47_out ? 2'b00 : 2'bz;  // Controlled_Buffer controlled_buffer_17
  or or_48 (or_48_out, and_110_out, and_111_out, and_112_out, and_103_out, and_117_out, and_118_out, and_119_out, and_113_out, and_108_out, and_109_out);
  assign FunSelB = or_48_out ? 2'b10 : 2'bz;  // Controlled_Buffer controlled_buffer_18
  or or_49 (or_49_out, T0, T1);
  assign FunselC = or_49_out ? 2'b10 : 2'bz;  // Controlled_Buffer controlled_buffer_19
  or or_50 (or_50_out, Rx_ARF_ARF, ARF_ARF_ARF);
  or or_51 (or_51_out, Rx_Rx_Rx, ARF_Rx_Rx);
  and and_120 (and_120_out, OP5, T3, or_52_out);
  or or_52 (or_52_out, Rx_Rx_ARF, Rx_ARF_Rx, ARF_ARF_Rx, ARF_Rx_ARF);
  and and_121 (and_121_out, OP5, T4, or_53_out);
  or or_53 (or_53_out, Rx_ARF_ARF, ARF_ARF_ARF);
  or or_54 (or_54_out, Rx_Rx_Rx, ARF_Rx_Rx);
  and and_122 (and_122_out, OP7, T3, or_55_out);
  or or_55 (or_55_out, Rx_Rx_ARF, Rx_ARF_Rx, ARF_ARF_Rx, ARF_Rx_ARF);
  and and_123 (and_123_out, OP7, T4, or_56_out);
  or or_56 (or_56_out, Rx_ARF_ARF, ARF_ARF_ARF);
  or or_57 (or_57_out, Rx_Rx_Rx, ARF_Rx_Rx);
  and and_124 (and_124_out, OP8, T3, or_58_out);
  or or_58 (or_58_out, Rx_Rx_ARF, Rx_ARF_Rx, ARF_ARF_Rx, ARF_Rx_ARF);
  and and_125 (and_125_out, OP8, T4, or_50_out);
  not not_68 (not_68_out, _16Bit_Data[10]);
  not not_69 (not_69_out, _16Bit_Data[10]);
  and and_126 (and_126_out, _16Bit_Data[10], SRCREG1[2]);
  not not_70 (not_70_out, _16Bit_Data[10]);
  and and_127 (and_127_out, _16Bit_Data[10], SRCREG1[2]);
  not not_71 (not_71_out, _16Bit_Data[10]);
  and and_128 (and_128_out, not_71_out, SRCREG1[2]);
  or or_59 (or_59_out, Rx_Rx_Rx, ARF_Rx_Rx);
  or or_60 (or_60_out, Rx_Rx_ARF, Rx_ARF_Rx, ARF_ARF_Rx, ARF_Rx_ARF);
  or or_61 (or_61_out, Rx_ARF_ARF, ARF_ARF_ARF);
  and and_129 (and_129_out, OP5, T2, or_51_out);
  and and_130 (and_130_out, OP7, T2, or_54_out);
  and and_131 (and_131_out, OP8, T2, or_57_out);
  not not_72 (not_72_out, _16Bit_Data[10]);
  and and_132 (and_132_out, _16Bit_Data[10], SRCREG1[2]);
  and and_133 (and_133_out, not_68_out, SRCREG1[2]);
  and and_134 (and_134_out, _16Bit_Data[10], SRCREG1[2]);
  and and_135 (and_135_out, not_69_out, SRCREG1[2]);
  or or_62 (or_62_out, and_126_out, and_136_out);
  and and_136 (and_136_out, not_70_out, SRCREG1[2]);
  or or_63 (or_63_out, and_127_out, and_128_out);
  and and_137 (and_137_out, OP4, T2, or_59_out);
  and and_138 (and_138_out, OP4, T3, or_60_out);
  and and_139 (and_139_out, OP4, T4, or_61_out);
  or or_64 (or_64_out, and_132_out, and_133_out);
  and and_140 (and_140_out, OP12, T2);
  or or_65 (or_65_out, and_134_out, and_135_out);
  and and_141 (and_141_out, OP10, T3);
  or or_66 (or_66_out, and_129_out, and_120_out, and_121_out);
  assign FunSelALU = or_67_out ? 4'b0100 : 4'bz;  // Controlled_Buffer controlled_buffer_20
  or or_67 (or_67_out, and_130_out, and_122_out, and_123_out);
  assign FunSelALU = or_68_out ? 4'b0110 : 4'bz;  // Controlled_Buffer controlled_buffer_21
  or or_68 (or_68_out, and_131_out, and_124_out, and_125_out);
  and and_142 (and_142_out, OP2, T2);
  and and_143 (and_143_out, OP3, T2, not_72_out, SRCREG1[2]);
  and and_144 (and_144_out, OP3, T2, _16Bit_Data[10], SRCREG1[2]);
  and and_145 (and_145_out, OP13_14, T3, or_64_out);
  and and_146 (and_146_out, OP6, T2, or_65_out);
  and and_147 (and_147_out, OP6, T3);
  and and_148 (and_148_out, OP9, T2, or_62_out);
  and and_149 (and_149_out, OP9, T3);
  and and_150 (and_150_out, OP10, T2, or_63_out);
  or or_69 (or_69_out, and_137_out, and_138_out, and_139_out);
  assign FunSelALU = or_66_out ? 4'b1000 : 4'bz;  // Controlled_Buffer controlled_buffer_22
  assign FunSelALU = or_70_out ? 4'b0000 : 4'bz;  // Controlled_Buffer controlled_buffer_23
  or or_70 (or_70_out, and_142_out, and_143_out, and_144_out, and_145_out, and_140_out);
  assign FunSelALU = or_71_out ? 4'b0010 : 4'bz;  // Controlled_Buffer controlled_buffer_24
  or or_71 (or_71_out, and_146_out, and_147_out);
  assign FunSelALU = or_72_out ? 4'b1010 : 4'bz;  // Controlled_Buffer controlled_buffer_25
  or or_72 (or_72_out, and_148_out, and_149_out);
  assign FunSelALU = or_73_out ? 4'b1011 : 4'bz;  // Controlled_Buffer controlled_buffer_26
  or or_73 (or_73_out, and_150_out, and_141_out);
  assign FunSelALU = or_69_out ? 4'b0111 : 4'bz;  // Controlled_Buffer controlled_buffer_27
  not not_73 (not_73_out, SRCREG1[2]);
  not not_74 (not_74_out, _16Bit_Data[10]);
  not not_75 (not_75_out, SRCREG1[2]);
  and and_151 (and_151_out, _16Bit_Data[10], not_73_out);
  and and_152 (and_152_out, not_74_out, not_75_out);
  and and_153 (and_153_out, _16Bit_Data[10], SRCREG1[2]);
  not not_76 (not_76_out, _16Bit_Data[10]);
  and and_154 (and_154_out, not_76_out, SRCREG1[2]);
  not not_77 (not_77_out, _16Bit_Data[10]);
  or or_74 (or_74_out, and_151_out, and_152_out);
  or or_75 (or_75_out, Rx_ARF_ARF, ARF_ARF_ARF);
  and and_155 (and_155_out, OP2, T2);
  or or_76 (or_76_out, and_153_out, and_154_out);
  and and_156 (and_156_out, _16Bit_Data[10], SRCREG1[2]);
  or or_77 (or_77_out, and_156_out, and_157_out);
  and and_157 (and_157_out, not_77_out, SRCREG1[2]);
  or or_78 (or_78_out, Rx_Rx_Rx, ARF_Rx_Rx);
  and and_158 (and_158_out, OP4_5_7_8, T4, or_75_out);
  not not_78 (not_78_out, _16Bit_Data[10]);
  and and_159 (and_159_out, OP3, T2, _16Bit_Data[10], SRCREG1[2]);
  and and_160 (and_160_out, OP6_9_10, T2, or_76_out);
  and and_161 (and_161_out, OP13_14, T3, or_77_out);
  and and_162 (and_162_out, OP4_5_7_8, T2, or_78_out);
  and and_163 (and_163_out, OP6_9_10, T3, or_74_out);
  buf or_79 (or_79_out, and_155_out);  // OR_Gate
  and and_164 (and_164_out, OP3, T2, not_78_out, SRCREG1[2]);
  or or_80 (or_80_out, Rx_Rx_ARF, ARF_Rx_ARF);
  or or_81 (or_81_out, Rx_ARF_Rx, ARF_ARF_Rx);
  assign OutASel = or_79_out ? {1'b0, _16Bit_Data[9:8]} : 3'bz;  // Controlled_Buffer controlled_buffer_28
  and and_165 (and_165_out, OP4_5_7_8, T3, or_80_out);
  and and_166 (and_166_out, OP12, T2);
  assign OutASel = or_82_out ? {1'b1, SRCREG1[1:0]} : 3'bz;  // Controlled_Buffer controlled_buffer_29
  or or_82 (or_82_out, and_163_out, and_158_out);
  and and_167 (and_167_out, OP4_5_7_8, T3, or_81_out);
  assign OutASel = or_83_out ? {1'b0, SRCREG2[1:0]} : 3'bz;  // Controlled_Buffer controlled_buffer_30
  buf or_83 (or_83_out, and_167_out);  // OR_Gate
  assign OutASel = or_84_out ? {1'b0, SRCREG1[1:0]} : 3'bz;  // Controlled_Buffer controlled_buffer_31
  or or_84 (or_84_out, and_164_out, and_159_out, and_160_out, and_161_out, and_162_out, and_165_out, and_166_out);
  or or_85 (or_85_out, Rx_Rx_Rx, ARF_Rx_Rx);
  and and_168 (and_168_out, OP4_5_7_8, T2, or_85_out);
  or or_86 (or_86_out, Rx_ARF_ARF, ARF_ARF_ARF);
  or or_87 (or_87_out, Rx_Rx_ARF, ARF_Rx_ARF);
  or or_88 (or_88_out, Rx_ARF_Rx, ARF_ARF_Rx);
  and and_169 (and_169_out, OP4_5_7_8, T4, or_86_out);
  and and_170 (and_170_out, OP4_5_7_8, T3, or_87_out);
  and and_171 (and_171_out, OP4_5_7_8, T3, or_88_out);
  or or_89 (or_89_out, and_169_out, and_170_out);
  buf or_90 (or_90_out, and_171_out);  // OR_Gate
  buf or_91 (or_91_out, and_168_out);  // OR_Gate
  assign OutBSel = or_89_out ? {1'b1, SRCREG2[1:0]} : 3'bz;  // Controlled_Buffer controlled_buffer_32
  assign OutBSel = or_90_out ? {1'b1, SRCREG1[1:0]} : 3'bz;  // Controlled_Buffer controlled_buffer_33
  assign OutBSel = or_91_out ? {1'b0, SRCREG2[1:0]} : 3'bz;  // Controlled_Buffer controlled_buffer_34
  and and_172 (and_172_out, _16Bit_Data[10], not_79_out);
  not not_79 (not_79_out, SRCREG1[2]);
  not not_80 (not_80_out, _16Bit_Data[10]);
  and and_173 (and_173_out, not_80_out, not_81_out);
  not not_81 (not_81_out, SRCREG1[2]);
  not not_82 (not_82_out, SRCREG1[2]);
  not not_83 (not_83_out, _16Bit_Data[10]);
  not not_84 (not_84_out, SRCREG1[2]);
  not not_85 (not_85_out, SRCREG1[2]);
  or or_92 (or_92_out, and_172_out, and_173_out);
  and and_174 (and_174_out, _16Bit_Data[10], not_82_out);
  and and_175 (and_175_out, not_83_out, not_84_out);
  or or_93 (or_93_out, Rx_Rx_ARF, ARF_Rx_ARF);
  or or_94 (or_94_out, Rx_ARF_ARF, ARF_ARF_ARF);
  not not_86 (not_86_out, _16Bit_Data[10]);
  not not_87 (not_87_out, SRCREG1[2]);
  or or_95 (or_95_out, and_174_out, and_175_out);
  or or_96 (or_96_out, Rx_ARF_Rx, Rx_ARF_ARF, ARF_ARF_ARF, ARF_ARF_Rx);
  and and_176 (and_176_out, OP4_5_7_8, T2, or_93_out);
  and and_177 (and_177_out, OP4_5_7_8, T3, or_94_out);
  and and_178 (and_178_out, OP3, T2, not_86_out, not_87_out);
  and and_179 (and_179_out, OP3, T2, _16Bit_Data[10], not_85_out);
  and and_180 (and_180_out, OP6_9_10, T2, or_92_out);
  and and_181 (and_181_out, OP13_14, T3, or_95_out);
  and and_182 (and_182_out, OP4_5_7_8, T2, or_96_out);
  assign OutCSel = or_97_out ? SRCREG2[1:0] : 2'bz;  // Controlled_Buffer controlled_buffer_35
  or or_97 (or_97_out, and_176_out, and_177_out);
  assign OutCSel = or_98_out ? SRCREG1[1:0] : 2'bz;  // Controlled_Buffer controlled_buffer_36
  or or_98 (or_98_out, and_178_out, and_179_out, and_180_out, and_181_out, and_182_out);
  not not_88 (not_88_out, _16Bit_Data[10]);
  not not_89 (not_89_out, _16Bit_Data[10]);
  and and_183 (and_183_out, OP1, not_88_out, T2);
  and and_184 (and_184_out, OP2, not_89_out, T2);
  and and_185 (and_185_out, OP11, T3);
  and and_186 (and_186_out, OP12, T2);
  or or_99 (or_99_out, T0, T1);
  assign OutDSel = or_99_out ? 2'b00 : 2'bz;  // Controlled_Buffer controlled_buffer_37
  assign OutDSel = or_100_out ? 2'b10 : 2'bz;  // Controlled_Buffer controlled_buffer_38
  or or_100 (or_100_out, and_183_out, and_184_out);
  assign OutDSel = or_101_out ? 2'b11 : 2'bz;  // Controlled_Buffer controlled_buffer_39
  or or_101 (or_101_out, and_185_out, and_186_out);
  not not_90 (not_90_out, SRCREG1[2]);
  not not_91 (not_91_out, _16Bit_Data[10]);
  not not_92 (not_92_out, SRCREG1[2]);
  not not_93 (not_93_out, SRCREG1[2]);
  not not_94 (not_94_out, SRCREG1[2]);
  and and_187 (and_187_out, _16Bit_Data[10], SRCREG1[2]);
  and and_188 (and_188_out, _16Bit_Data[10], not_90_out);
  and and_189 (and_189_out, not_91_out, not_92_out);
  and and_190 (and_190_out, _16Bit_Data[10], not_93_out);
  or or_102 (or_102_out, Rx_ARF_ARF, ARF_ARF_ARF);
  and and_191 (and_191_out, OP4_5_7_8, T3, or_103_out);
  or or_103 (or_103_out, Rx_Rx_ARF, Rx_ARF_Rx);
  not not_95 (not_95_out, SRCREG1[2]);
  or or_104 (or_104_out, and_188_out, and_189_out);
  or or_105 (or_105_out, ARF_Rx_ARF, Rx_Rx_ARF, Rx_ARF_Rx, Rx_ARF_ARF, ARF_ARF_ARF, ARF_ARF_Rx);
  and and_192 (and_192_out, OP4_5_7_8, T3, or_102_out);
  not not_96 (not_96_out, _16Bit_Data[10]);
  and and_193 (and_193_out, OP3, T2, _16Bit_Data[10], SRCREG1[2]);
  and and_194 (and_194_out, OP6_9_10, T2, _16Bit_Data[10], SRCREG1[2]);
  and and_195 (and_195_out, OP6_9_10, T3, _16Bit_Data[10], not_94_out);
  and and_196 (and_196_out, OP13_14, T3, and_187_out);
  and and_197 (and_197_out, OP4_5_7_8, T2, Rx_Rx_Rx);
  and and_198 (and_198_out, OP4_5_7_8, T4, Rx_ARF_ARF);
  and and_199 (and_199_out, OP3, T2, _16Bit_Data[10], not_95_out);
  and and_200 (and_200_out, OP6_9_10, T2, or_104_out);
  and and_201 (and_201_out, OP13_14, T3, and_190_out);
  and and_202 (and_202_out, OP4_5_7_8, T2, or_105_out);
  and and_203 (and_203_out, OP1, not_96_out, T2);
  and and_204 (and_204_out, OP11, T3);
  or or_106 (or_106_out, and_199_out, and_200_out, and_201_out, and_202_out, and_192_out);
  assign MuxASel = and_205_out ? 2'b10 : 2'bz;  // Controlled_Buffer controlled_buffer_40
  and and_205 (and_205_out, OP1, _16Bit_Data[10], T2);
  assign MuxASel = or_107_out ? 2'b01 : 2'bz;  // Controlled_Buffer controlled_buffer_41
  or or_107 (or_107_out, and_203_out, and_204_out);
  assign MuxASel = or_108_out ? 2'b00 : 2'bz;  // Controlled_Buffer controlled_buffer_42
  or or_108 (or_108_out, and_193_out, and_194_out, and_195_out, and_196_out, and_197_out, and_191_out, and_198_out);
  assign MuxASel = or_106_out ? 2'b11 : 2'bz;  // Controlled_Buffer controlled_buffer_43
  not not_97 (not_97_out, _16Bit_Data[10]);
  not not_98 (not_98_out, SRCREG1[2]);
  not not_99 (not_99_out, _16Bit_Data[10]);
  and and_206 (and_206_out, not_99_out, SRCREG1[2]);
  not not_100 (not_100_out, _16Bit_Data[10]);
  not not_101 (not_101_out, _16Bit_Data[10]);
  not not_102 (not_102_out, SRCREG1[2]);
  and and_207 (and_207_out, not_97_out, not_98_out);
  not not_103 (not_103_out, _16Bit_Data[10]);
  not not_104 (not_104_out, _16Bit_Data[10]);
  not not_105 (not_105_out, SRCREG1[2]);
  and and_208 (and_208_out, not_100_out, SRCREG1[2]);
  or or_109 (or_109_out, ARF_ARF_Rx, ARF_Rx_ARF);
  not not_106 (not_106_out, Z);
  and and_209 (and_209_out, OP3, T2, not_101_out, not_102_out);
  and and_210 (and_210_out, OP13_14, T3, and_207_out);
  and and_211 (and_211_out, OP3, T2, not_103_out, SRCREG1[2]);
  and and_212 (and_212_out, OP6_9_10, T2, and_206_out);
  and and_213 (and_213_out, OP6_9_10, T3, not_104_out, not_105_out);
  and and_214 (and_214_out, OP13_14, T3, and_208_out);
  and and_215 (and_215_out, OP4_5_7_8, T2, ARF_Rx_Rx);
  and and_216 (and_216_out, OP4_5_7_8, T3, or_109_out);
  and and_217 (and_217_out, OP4_5_7_8, T4, ARF_ARF_ARF);
  and and_218 (and_218_out, OP0, T2);
  and and_219 (and_219_out, OP15, _16Bit_Data[10], T2, not_106_out);
  or or_110 (or_110_out, and_209_out, and_210_out);
  or or_111 (or_111_out, and_211_out, and_212_out, and_213_out, and_214_out, and_215_out, and_216_out, and_217_out);
  assign MuxBSel = or_112_out ? 2'b10 : 2'bz;  // Controlled_Buffer controlled_buffer_44
  or or_112 (or_112_out, and_218_out, and_219_out);
  assign MuxBSel = or_110_out ? 2'b11 : 2'bz;  // Controlled_Buffer controlled_buffer_45
  assign MuxBSel = or_111_out ? 2'b00 : 2'bz;  // Controlled_Buffer controlled_buffer_46
  not not_107 (not_107_out, SRCREG1[2]);
  not not_108 (not_108_out, _16Bit_Data[10]);
  not not_109 (not_109_out, SRCREG1[2]);
  and and_220 (and_220_out, _16Bit_Data[10], not_107_out);
  and and_221 (and_221_out, not_108_out, not_109_out);
  or or_113 (or_113_out, Rx_ARF_Rx, Rx_ARF_ARF, ARF_ARF_ARF, ARF_ARF_Rx);
  or or_114 (or_114_out, and_220_out, and_221_out);
  and and_222 (and_222_out, OP4_5_7_8, T2, or_113_out);
  or or_115 (or_115_out, Rx_Rx_ARF, ARF_Rx_ARF);
  or or_116 (or_116_out, Rx_ARF_ARF, ARF_ARF_ARF);
  and and_223 (and_223_out, OP6_9_10, T2, or_114_out);
  and and_224 (and_224_out, OP4_5_7_8, T2, or_115_out);
  and and_225 (and_225_out, OP4_5_7_8, T3, or_116_out);
  assign TmpSelA = or_117_out ? New_TmpSel : 4'bz;  // Controlled_Buffer controlled_buffer_47
  or or_117 (or_117_out, and_223_out, and_222_out);
  assign TmpSelA = or_118_out ? New_TmpSel_2 : 4'bz;  // Controlled_Buffer controlled_buffer_48
  or or_118 (or_118_out, and_224_out, and_225_out);

  // Other names for the same wires on the sheet: DESTREG[3:0] = _16Bit_Data[11:8]; DESTREG_R[1:0] = _16Bit_Data[9:8];
  //   Others[11:0] = _16Bit_Data[11:0]; RegSel[1:0] = _16Bit_Data[9:8]; SRCREG_2_R[1:0] = SRCREG2[1:0];
  //   SRCREG_1_R[1:0] = SRCREG1[1:0]; Address[7:0] = _16Bit_Data[7:0]; AddMode = _16Bit_Data[10];
  //   DESTREG_A = _16Bit_Data[10]; OpCode[3:0] = _16Bit_Data[15:12]; SRCREG_1_A = SRCREG1[2]; SRCREG_2_A = SRCREG2[2]

  // Notes on the sheet:
  //   L/H
  //   ENABLE
  //   FINISH
  //   LOAD
  //   READ
  //   RegSelA
  //   DEST İŞLEMİ
  //   SRC_1
  //   Select SP Register
  //   RegSelB
  //   FunSelA
  //   FunSelB
  //   FunSelC
  //   FunSelALU
  //   OutASel
  //   OutBSel
  //   OutCSel
  //   OutDSel
  //   MuxASel
  //   MuxBSel
  //   TmpSelA
endmodule
